# Fritzing sketch Schematics (saved by Fritzing 0.9.9b)

parts:
  U1 = ESP8266 NodeMCU LoLin module
  LCD2004-I2C1 = LCD2004-I2C
  M1 = Humidity and Temperature Sensor DHT11
  S1 = Pushbutton [package="[THT]"]
  LED1 = smd LED [color="Red (633nm)" package="0603 [SMD]"]

nets:
  N1: U1.D1, LCD2004-I2C1.SCL
  N2: U1.D2, LCD2004-I2C1.SDA
  N3: U1.D4, LED1.cathode
  VCC: U1.D5, U1.Vin, LCD2004-I2C1.VCC, M1.Vcc, M1.Data
  GND: U1.D7, U1.GND, LCD2004-I2C1.GND, M1.GND, S1.Pin_3, S1.Pin_4, LED1.anode

notes:
  Made by: Zhu Jiatong

custom parts:
  ESP8266 NodeMCU LoLin module: ESP8266 based NodeMCU
  LCD2004-I2C: A standard character display with 4x20 characters. Comes in many colors with LCM2004 IIC attached.
  Humidity and Temperature Sensor DHT11: Digital relative humidity & temperature sensor DHT11
